// Logisim project Exo1_TP1.circ as structural Verilog: 2 circuits, main circuit DemieAdi
module DemieAdi (
  input  A,
  input  B,
  output SOMME,
  output reste
);

  xor xor_1 (SOMME, A, B);
  and and_1 (reste, A, B);
endmodule

module AddComp (
  input  A,
  input  B,
  output \xor ,
  output a_b
);

  or _1 (\xor , A, B);
  and \and  (a_b, A, B);
endmodule
