// Logisim project Exo2_TP1.circ as structural Verilog: 1 circuit, main circuit AdiComp
module AdiComp (
  input  A,
  input  B,
  input  Cin,
  output A_B_cin,
  output cout
);

  wire and_1_out, and_2_out, xor_1_out;

  xor xor_1 (xor_1_out, A, B);
  xor xor_2 (A_B_cin, xor_1_out, Cin);
  and and_1 (and_1_out, Cin, xor_1_out);
  and and_2 (and_2_out, B, A);
  or or_1 (cout, and_1_out, and_2_out);
endmodule
