// Logisim project Exo3_TP1.circ as structural Verilog: 1 circuit, main circuit Addi8bits
module Addi8bits (
  input  A,
  input  A_2,
  input  B,
  input  A_3,
  input  B_2,
  input  B_3,
  input  A_4,
  input  B_4,
  input  A_5,
  input  B_5,
  input  A_6,
  input  B_6,
  input  A_7,
  input  B_7,
  input  A_8,
  input  B_8,
  output out_17,
  output A_B_cin,
  output A_B_cin_2,
  output A_B_cin_3,
  output A_B_cin_4,
  output out_22,
  output out_23,
  output out_24,
  output out_25
);

  wire and_1_out, and_2_out, and_3_out, and_4_out, and_5_out, and_6_out, and_7_out, and_8_out, and_9_out,
       and_10_out, and_11_out, and_12_out, and_13_out, and_14_out, and_15_out, or_2_out, or_3_out, or_4_out,
       or_5_out, or_6_out, or_7_out, xor_2_out, xor_5_out, xor_6_out, xor_9_out, xor_10_out, xor_13_out,
       xor_14_out;

  xor xor_1 (out_17, A_2, B_2);
  and and_1 (and_1_out, A_2, B_2);
  xor xor_2 (xor_2_out, A, B);
  xor xor_3 (A_B_cin, xor_2_out, and_1_out);
  and and_2 (and_2_out, and_1_out, xor_2_out);
  and and_3 (and_3_out, A, B);
  or or_1 (out_25, and_4_out, and_5_out);
  or or_2 (or_2_out, and_2_out, and_3_out);
  xor xor_4 (out_24, xor_5_out, or_4_out);
  and and_4 (and_4_out, or_4_out, xor_5_out);
  and and_5 (and_5_out, A_8, B_8);
  xor xor_5 (xor_5_out, A_8, B_8);
  xor xor_6 (xor_6_out, A_3, B_3);
  xor xor_7 (A_B_cin_2, xor_6_out, or_2_out);
  and and_6 (and_6_out, or_2_out, xor_6_out);
  and and_7 (and_7_out, A_3, B_3);
  or or_3 (or_3_out, and_6_out, and_7_out);
  or or_4 (or_4_out, and_8_out, and_9_out);
  xor xor_8 (out_23, xor_10_out, or_6_out);
  and and_8 (and_8_out, or_6_out, xor_10_out);
  and and_9 (and_9_out, A_7, B_7);
  xor xor_9 (xor_9_out, A_4, B_4);
  xor xor_10 (xor_10_out, A_7, B_7);
  xor xor_11 (A_B_cin_3, xor_9_out, or_3_out);
  and and_10 (and_10_out, or_3_out, xor_9_out);
  and and_11 (and_11_out, A_4, B_4);
  or or_5 (or_5_out, and_10_out, and_11_out);
  or or_6 (or_6_out, and_12_out, and_13_out);
  xor xor_12 (out_22, xor_14_out, or_7_out);
  and and_12 (and_12_out, or_7_out, xor_14_out);
  and and_13 (and_13_out, A_6, B_6);
  xor xor_13 (xor_13_out, A_5, B_5);
  xor xor_14 (xor_14_out, A_6, B_6);
  xor xor_15 (A_B_cin_4, xor_13_out, or_5_out);
  and and_14 (and_14_out, or_5_out, xor_13_out);
  and and_15 (and_15_out, A_5, B_5);
  or or_7 (or_7_out, and_14_out, and_15_out);
endmodule
