// Logisim project Exo4_TP1.circ as structural Verilog: 1 circuit, main circuit main
module main (
  input  A,
  input  B,
  input  A_2,
  input  A_3,
  input  B_2,
  input  B_3,
  input  A_4,
  input  B_4,
  input  A_5,
  input  B_5,
  input  A_6,
  input  B_6,
  input  A_7,
  input  B_7,
  input  A_8,
  input  B_8,
  output out_17,
  output out_18,
  output out_19,
  output out_20,
  output out_21,
  output out_22,
  output out_23,
  output out_24,
  output out_25
);

  wire and_1_out, and_3_out, and_4_out, and_5_out, and_6_out, and_7_out, and_8_out, and_9_out, and_10_out,
       and_11_out, and_12_out, and_13_out, and_14_out, and_15_out, and_16_out, not_1_out, not_2_out,
       not_3_out, not_4_out, not_5_out, not_6_out, not_7_out, not_8_out, not_9_out, not_10_out, not_11_out,
       not_12_out, not_13_out, not_14_out, not_15_out, or_3_out, xor_3_out, xor_5_out, xor_6_out, xor_8_out,
       xor_9_out, xor_11_out, xor_13_out, xor_14_out, xor_15_out, xor_18_out, xor_19_out, xor_21_out;

  not not_1 (not_1_out, A_2);
  xor xor_1 (out_18, A_2, B_2);
  and and_1 (and_1_out, not_1_out, B_2);
  // XOR_Gate xor_2 is placed but not wired
  not not_2 (not_2_out, xor_3_out);
  not not_3 (not_3_out, A);
  // AND_Gate and_2 is placed but not wired
  xor xor_3 (xor_3_out, A, B);
  and and_3 (and_3_out, not_2_out, and_1_out);
  and and_4 (and_4_out, not_3_out, B);
  // OR_Gate or_1 is placed but not wired
  xor xor_4 (out_17, xor_3_out, and_1_out);
  xor xor_5 (xor_5_out, and_3_out, and_4_out);
  xor xor_6 (xor_6_out, A_3, B_3);
  not not_4 (not_4_out, xor_6_out);
  and and_5 (and_5_out, not_4_out, xor_5_out);
  not not_5 (not_5_out, A_3);
  and and_6 (and_6_out, not_5_out, B_3);
  xor xor_7 (out_19, xor_6_out, xor_5_out);
  xor xor_8 (xor_8_out, and_5_out, and_6_out);
  xor xor_9 (xor_9_out, A_4, B_4);
  not not_6 (not_6_out, xor_9_out);
  and and_7 (and_7_out, not_6_out, xor_8_out);
  not not_7 (not_7_out, A_4);
  and and_8 (and_8_out, not_7_out, B_4);
  xor xor_10 (out_20, xor_9_out, xor_8_out);
  xor xor_11 (xor_11_out, and_7_out, and_8_out);
  xor xor_12 (out_24, xor_13_out, or_3_out);
  or or_2 (out_25, and_9_out, and_10_out);
  not not_8 (not_8_out, xor_14_out);
  not not_9 (not_9_out, A_5);
  xor xor_13 (xor_13_out, A_8, B_8);
  not not_10 (not_10_out, xor_13_out);
  and and_9 (and_9_out, not_10_out, or_3_out);
  and and_10 (and_10_out, not_11_out, B_8);
  xor xor_14 (xor_14_out, A_5, B_5);
  and and_11 (and_11_out, not_8_out, xor_11_out);
  xor xor_15 (xor_15_out, and_11_out, and_12_out);
  and and_12 (and_12_out, not_9_out, B_5);
  not not_11 (not_11_out, A_8);
  xor xor_16 (out_21, xor_14_out, xor_11_out);
  xor xor_17 (out_23, xor_19_out, xor_21_out);
  or or_3 (or_3_out, and_15_out, and_16_out);
  xor xor_18 (xor_18_out, A_6, B_6);
  not not_12 (not_12_out, xor_18_out);
  and and_13 (and_13_out, not_12_out, xor_15_out);
  not not_13 (not_13_out, A_6);
  and and_14 (and_14_out, not_13_out, B_6);
  xor xor_19 (xor_19_out, A_7, B_7);
  not not_14 (not_14_out, xor_19_out);
  and and_15 (and_15_out, not_14_out, xor_21_out);
  not not_15 (not_15_out, A_7);
  and and_16 (and_16_out, not_15_out, B_7);
  xor xor_20 (out_22, xor_18_out, xor_15_out);
  xor xor_21 (xor_21_out, and_13_out, and_14_out);
endmodule
