// Logisim project Exo6_TP1.circ as structural Verilog: 1 circuit, main circuit main
module main (
  input  in_1,
  input  in_2,
  input  in_3,
  input  in_4,
  input  in_5,
  input  in_6,
  input  in_7,
  input  in_8,
  input  in_9,
  input  in_10,
  output out_11,
  output out_12,
  output out_13,
  output out_14,
  output out_15,
  output out_16,
  output out_17,
  output out_18,
  output out_19
);

  wire and_1_out, and_2_out, and_3_out, and_4_out, and_5_out, and_6_out, and_7_out, and_8_out, and_9_out,
       and_10_out, and_11_out, and_12_out, and_13_out, and_14_out, and_15_out, and_16_out, and_17_out,
       and_18_out, and_19_out, and_20_out, and_21_out, and_22_out, and_23_out, and_24_out, and_25_out,
       and_26_out, and_27_out, and_28_out, and_29_out, and_30_out, and_31_out, and_32_out, and_33_out,
       and_34_out, and_35_out, and_36_out, and_37_out, and_38_out, and_39_out, and_40_out, and_41_out,
       and_42_out, and_43_out, not_1_out, not_2_out, or_2_out, or_3_out, or_4_out, or_5_out, or_6_out,
       or_7_out, or_8_out, or_9_out, or_10_out, or_11_out, or_12_out, or_13_out, or_14_out, or_15_out,
       or_16_out, or_17_out, or_18_out, or_19_out, xor_2_out, xor_4_out, xor_6_out, xor_8_out, xor_10_out,
       xor_12_out, xor_14_out;

  or or_1 (out_11, and_3_out, and_4_out);
  not not_1 (not_1_out, in_9);
  and and_1 (and_1_out, in_1, in_9);
  not not_2 (not_2_out, in_10);
  and and_2 (and_2_out, and_5_out, in_10);
  xor xor_1 (out_14, xor_2_out, or_4_out);
  and and_3 (and_3_out, or_4_out, xor_2_out);
  and and_4 (and_4_out, in_1, and_6_out);
  and and_5 (and_5_out, not_1_out, in_2);
  or or_2 (or_2_out, and_1_out, and_8_out);
  and and_6 (and_6_out, not_2_out, or_2_out);
  or or_3 (or_3_out, and_2_out, and_9_out);
  xor xor_2 (xor_2_out, in_1, and_6_out);
  and and_7 (and_7_out, in_2, in_9);
  and and_8 (and_8_out, not_1_out, in_3);
  and and_9 (and_9_out, not_2_out, or_5_out);
  and and_10 (and_10_out, or_2_out, in_10);
  or or_4 (or_4_out, and_13_out, and_14_out);
  and and_11 (and_11_out, in_3, in_9);
  or or_5 (or_5_out, and_7_out, and_15_out);
  and and_12 (and_12_out, or_5_out, in_10);
  or or_6 (or_6_out, and_10_out, and_18_out);
  xor xor_3 (out_19, xor_4_out, or_13_out);
  and and_13 (and_13_out, or_13_out, xor_4_out);
  and and_14 (and_14_out, in_2, or_3_out);
  and and_15 (and_15_out, not_1_out, in_4);
  and and_16 (and_16_out, in_4, in_9);
  or or_7 (or_7_out, and_11_out, and_19_out);
  and and_17 (and_17_out, or_7_out, in_10);
  and and_18 (and_18_out, not_2_out, or_7_out);
  or or_8 (or_8_out, and_12_out, and_21_out);
  xor xor_4 (xor_4_out, in_2, or_3_out);
  and and_19 (and_19_out, not_1_out, in_5);
  and and_20 (and_20_out, in_5, in_9);
  or or_9 (or_9_out, and_16_out, and_23_out);
  and and_21 (and_21_out, not_2_out, or_9_out);
  and and_22 (and_22_out, or_9_out, in_10);
  or or_10 (or_10_out, and_17_out, and_24_out);
  and and_23 (and_23_out, not_1_out, in_6);
  or or_11 (or_11_out, and_20_out, and_25_out);
  and and_24 (and_24_out, not_2_out, or_11_out);
  or or_12 (or_12_out, and_22_out, and_28_out);
  or or_13 (or_13_out, and_29_out, and_30_out);
  and and_25 (and_25_out, not_1_out, in_7);
  and and_26 (and_26_out, in_6, in_9);
  and and_27 (and_27_out, or_11_out, in_10);
  and and_28 (and_28_out, not_2_out, or_14_out);
  xor xor_5 (out_15, xor_6_out, or_16_out);
  and and_29 (and_29_out, or_16_out, xor_6_out);
  and and_30 (and_30_out, in_3, or_6_out);
  and and_31 (and_31_out, in_7, in_9);
  or or_14 (or_14_out, and_26_out, and_33_out);
  and and_32 (and_32_out, or_14_out, in_10);
  or or_15 (or_15_out, and_27_out, and_34_out);
  xor xor_6 (xor_6_out, in_3, or_6_out);
  and and_33 (and_33_out, not_1_out, in_8);
  and and_34 (and_34_out, not_2_out, and_31_out);
  or or_16 (or_16_out, and_35_out, and_36_out);
  xor xor_7 (out_16, xor_8_out, or_17_out);
  and and_35 (and_35_out, or_17_out, xor_8_out);
  and and_36 (and_36_out, in_4, or_8_out);
  xor xor_8 (xor_8_out, in_4, or_8_out);
  or or_17 (or_17_out, and_37_out, and_38_out);
  xor xor_9 (out_17, xor_10_out, or_18_out);
  and and_37 (and_37_out, or_18_out, xor_10_out);
  and and_38 (and_38_out, in_5, or_10_out);
  xor xor_10 (xor_10_out, in_5, or_10_out);
  or or_18 (or_18_out, and_39_out, and_40_out);
  xor xor_11 (out_18, xor_12_out, or_19_out);
  and and_39 (and_39_out, or_19_out, xor_12_out);
  and and_40 (and_40_out, in_6, or_12_out);
  xor xor_12 (xor_12_out, in_6, or_12_out);
  or or_19 (or_19_out, and_41_out, and_42_out);
  xor xor_13 (out_12, xor_14_out, and_43_out);
  and and_41 (and_41_out, and_43_out, xor_14_out);
  and and_42 (and_42_out, in_7, or_15_out);
  xor xor_14 (xor_14_out, in_7, or_15_out);
  xor xor_15 (out_13, in_8, and_32_out);
  and and_43 (and_43_out, in_8, and_32_out);
endmodule
