// Logisim project Multiplexeur.circ as structural Verilog: 1 circuit, main circuit main
module main (
  input  A,
  input  B,
  input  C,
  input  D,
  output S
);

  wire and_1_out, and_2_out, and_3_out, and_4_out, and_5_out, and_6_out, and_7_out, and_8_out, and_9_out,
       and_10_out, and_11_out, and_12_out, and_13_out, and_14_out, and_15_out, and_16_out, not_1_out,
       not_2_out, not_3_out, not_4_out, not_5_out;

  not not_1 (not_1_out, 1'b1);
  not not_2 (not_2_out, A);
  not not_3 (not_3_out, B);
  not not_4 (not_4_out, C);
  not not_5 (not_5_out, D);
  and and_1 (and_1_out, 1'b1, not_2_out, not_3_out, not_4_out, not_5_out);
  and and_2 (and_2_out, 1'b1, not_2_out, not_3_out, not_4_out, D);
  and and_3 (and_3_out, 1'b1, not_2_out, not_3_out, C, not_5_out);
  and and_4 (and_4_out, not_1_out, not_2_out, not_3_out, C, D);
  and and_5 (and_5_out, 1'b1, not_2_out, B, not_4_out, not_5_out);
  and and_6 (and_6_out, not_1_out, not_2_out, B, not_4_out, D);
  and and_7 (and_7_out, not_1_out, not_2_out, B, C, not_5_out);
  and and_8 (and_8_out, 1'b1, not_2_out, B, C, D);
  and and_9 (and_9_out, 1'b1, A, not_3_out, not_4_out, not_5_out);
  and and_10 (and_10_out, not_1_out, A, not_3_out, not_4_out, D);
  and and_11 (and_11_out, not_1_out, A, not_3_out, C, not_5_out);
  and and_12 (and_12_out, 1'b1, A, not_3_out, C, D);
  and and_13 (and_13_out, not_1_out, A, B, not_4_out, not_5_out);
  and and_14 (and_14_out, 1'b1, A, B, not_4_out, D);
  and and_15 (and_15_out, 1'b1, A, B, C, not_5_out);
  and and_16 (and_16_out, not_1_out, A, B, C, D);
  or or_1 (S, and_1_out, and_2_out, and_3_out, and_4_out, and_5_out, and_6_out, and_7_out, and_8_out, and_9_out, and_10_out, and_11_out, and_12_out, and_13_out, and_14_out, and_15_out, and_16_out);
endmodule
