// Logisim project codeur+additionneur.circ as structural Verilog: 1 circuit, main circuit main
module main (
  input  E0,
  input  E1,
  input  E2,
  input  E3,
  input  E4,
  input  E5,
  input  E6,
  input  E7,
  input  E8,
  input  E9,
  input  E10,
  input  E11,
  input  A,
  input  B,
  input  E12,
  input  A_2,
  input  B_2,
  input  E13,
  input  A_3,
  input  B_3,
  input  E14,
  input  E15,
  input  E0_2,
  input  E1_2,
  input  E2_2,
  input  E3_2,
  input  E4_2,
  input  E5_2,
  input  E6_2,
  input  E7_2,
  input  E8_2,
  input  E9_2,
  input  E10_2,
  input  E11_2,
  input  E12_2,
  input  E13_2,
  input  E14_2,
  input  E15_2,
  output out_39,
  output A_B_cin,
  output A_B_cin_2,
  output A_B_cin_3,
  output A_B_cin_4,
  output A_B_cin_5,
  output A_B_cin_6
);

  wire and_1_out, and_2_out, and_3_out, and_4_out, and_5_out, and_6_out, and_7_out, and_8_out, and_9_out,
       and_10_out, and_11_out, and_12_out, and_13_out, or_1_out, or_2_out, or_3_out, or_4_out, or_5_out,
       S0_2_out, S0_out, S1_2_out, S1_out, S2_2_out, S2_out, S3_2_out, S3_out, xor_2_out, xor_3_out,
       xor_4_out, xor_8_out, xor_10_out, xor_12_out;

  or S0 (S0_out, E1_2, E3_2, E5_2, E7_2, E9_2, E11_2, E13_2, E15_2);
  or S1 (S1_out, E2_2, E3_2, E6_2, E7_2, E10_2, E11_2, E14_2, E15_2);
  or S2 (S2_out, E5_2, E4_2, E6_2, E7_2, E12_2, E13_2, E14_2, E15_2);
  or S3 (S3_out, E9_2, E10_2, E11_2, E12_2, E13_2, E14_2, E15_2, E8_2);
  or S0_2 (S0_2_out, E1, E3, E5, E7, E9, E11, E13, E15);
  or S1_2 (S1_2_out, E2, E3, E6, E7, E10, E11, E14, E15);
  or S2_2 (S2_2_out, E5, E4, E6, E7, E12, E13, E14, E15);
  or S3_2 (S3_2_out, E9, E10, E11, E12, E13, E14, E15, E8);
  xor xor_1 (out_39, S0_2_out, S0_out);
  and and_1 (and_1_out, S0_2_out, S0_out);
  xor xor_2 (xor_2_out, S1_2_out, S1_out);
  xor xor_3 (xor_3_out, S2_2_out, S2_out);
  xor xor_4 (xor_4_out, S3_2_out, S3_out);
  xor xor_5 (A_B_cin, xor_2_out, and_1_out);
  and and_2 (and_2_out, and_1_out, xor_2_out);
  and and_3 (and_3_out, S1_2_out, S1_out);
  xor xor_6 (A_B_cin_2, xor_3_out, or_1_out);
  and and_4 (and_4_out, or_1_out, xor_3_out);
  and and_5 (and_5_out, S2_2_out, S2_out);
  xor xor_7 (A_B_cin_3, xor_4_out, or_2_out);
  and and_6 (and_6_out, or_2_out, xor_4_out);
  and and_7 (and_7_out, S3_2_out, S3_out);
  or or_1 (or_1_out, and_2_out, and_3_out);
  or or_2 (or_2_out, and_4_out, and_5_out);
  or or_3 (or_3_out, and_6_out, and_7_out);
  xor xor_8 (xor_8_out, A, B);
  xor xor_9 (A_B_cin_4, xor_8_out, or_3_out);
  and and_8 (and_8_out, or_3_out, xor_8_out);
  and and_9 (and_9_out, A, B);
  or or_4 (or_4_out, and_8_out, and_9_out);
  xor xor_10 (xor_10_out, A_2, B_2);
  xor xor_11 (A_B_cin_5, xor_10_out, or_4_out);
  and and_10 (and_10_out, or_4_out, xor_10_out);
  and and_11 (and_11_out, A_2, B_2);
  or or_5 (or_5_out, and_10_out, and_11_out);
  xor xor_12 (xor_12_out, A_3, B_3);
  xor xor_13 (A_B_cin_6, xor_12_out, or_5_out);
  and and_12 (and_12_out, or_5_out, xor_12_out);
  and and_13 (and_13_out, A_3, B_3);
  // OR_Gate or_6 has open pins: in0=and_12_out, in1=and_13_out, out=open
endmodule
