// Logisim project codeur+decaleur.circ as structural Verilog: 1 circuit, main circuit main
module main (
  input  E0,
  input  E1,
  input  E2,
  input  E3,
  input  E4,
  input  E5,
  input  in_7,
  input  in_8,
  input  in_9,
  input  in_10,
  input  in_11,
  input  E6,
  input  E7,
  input  E8,
  input  E9,
  input  E10,
  input  E11,
  input  E12,
  input  E13,
  input  E14,
  input  E15,
  output out_22,
  output out_23,
  output out_24,
  output out_25,
  output out_26,
  output out_27,
  output out_28,
  output out_29
);

  wire and_1_out, and_3_out, and_4_out, and_5_out, and_6_out, and_7_out, and_8_out, and_9_out, and_10_out,
       and_11_out, and_12_out, and_14_out, not_1_out, S0_out, S1_out, S2_out, S3_out;

  or S0 (S0_out, E1, E3, E5, E7, E9, E11, E13, E15);
  or S1 (S1_out, E2, E3, E6, E7, E10, E11, E14, E15);
  or S2 (S2_out, E5, E4, E6, E7, E12, E13, E14, E15);
  or S3 (S3_out, E9, E10, E11, E12, E13, E14, E15, E8);
  not not_1 (not_1_out, in_11);
  and and_1 (and_1_out, S0_out, in_11);
  and and_2 (out_22, not_1_out, S1_out);
  or or_1 (out_23, and_1_out, and_4_out);
  and and_3 (and_3_out, S1_out, in_11);
  and and_4 (and_4_out, not_1_out, S2_out);
  and and_5 (and_5_out, S2_out, in_11);
  or or_2 (out_24, and_3_out, and_6_out);
  and and_6 (and_6_out, not_1_out, S3_out);
  and and_7 (and_7_out, S3_out, in_11);
  or or_3 (out_25, and_5_out, and_9_out);
  and and_8 (and_8_out, in_7, in_11);
  and and_9 (and_9_out, not_1_out, in_7);
  or or_4 (out_26, and_7_out, and_10_out);
  and and_10 (and_10_out, not_1_out, in_8);
  or or_5 (out_27, and_8_out, and_12_out);
  and and_11 (and_11_out, in_8, in_11);
  and and_12 (and_12_out, not_1_out, in_9);
  and and_13 (out_29, in_9, in_11);
  or or_6 (out_28, and_11_out, and_14_out);
  and and_14 (and_14_out, not_1_out, in_10);
endmodule
