// Logisim project codeur+detecteur.circ as structural Verilog: 1 circuit, main circuit main
module main (
  input  E0,
  input  E1,
  input  E2,
  input  E3,
  input  E4,
  input  E5,
  input  E6,
  input  E7,
  input  E8,
  input  E9,
  input  E10,
  input  E11,
  input  E12,
  input  E13,
  input  E14,
  input  E15,
  output S
);

  wire and_1_out, and_2_out, and_3_out, and_4_out, and_5_out, and_6_out, and_7_out, and_8_out, and_9_out,
       and_10_out, and_11_out, and_12_out, and_13_out, and_14_out, and_15_out, and_16_out, not_1_out,
       not_2_out, not_3_out, not_4_out, S0_out, S1_out, S2_out, S3_out;

  or S0 (S0_out, E1, E3, E5, E7, E9, E11, E13, E15);
  or S1 (S1_out, E2, E3, E6, E7, E10, E11, E14, E15);
  or S2 (S2_out, E5, E4, E6, E7, E12, E13, E14, E15);
  or S3 (S3_out, E9, E10, E11, E12, E13, E14, E15, E8);
  not not_1 (not_1_out, S0_out);
  not not_2 (not_2_out, S1_out);
  not not_3 (not_3_out, S2_out);
  not not_4 (not_4_out, S3_out);
  and and_1 (and_1_out, 1'b1, not_1_out, not_2_out, not_3_out, not_4_out);
  and and_2 (and_2_out, 1'b1, not_1_out, not_2_out, not_3_out, S3_out);
  and and_3 (and_3_out, 1'b1, not_1_out, not_2_out, S2_out, not_4_out);
  and and_4 (and_4_out, 1'b1, not_1_out, not_2_out, S2_out, S3_out);
  and and_5 (and_5_out, 1'b1, not_1_out, S1_out, not_3_out, not_4_out);
  and and_6 (and_6_out, 1'b1, not_1_out, S1_out, not_3_out, S3_out);
  and and_7 (and_7_out, 1'b1, not_1_out, S1_out, S2_out, not_4_out);
  and and_8 (and_8_out, 1'b1, not_1_out, S1_out, S2_out, S3_out);
  and and_9 (and_9_out, 1'b1, S0_out, not_2_out, not_3_out, not_4_out);
  and and_10 (and_10_out, 1'b1, S0_out, not_2_out, not_3_out, S3_out);
  and and_11 (and_11_out, 1'b1, S0_out, not_2_out, S2_out, not_4_out);
  and and_12 (and_12_out, 1'b1, S0_out, not_2_out, S2_out, S3_out);
  and and_13 (and_13_out, 1'b1, S0_out, S1_out, not_3_out, not_4_out);
  and and_14 (and_14_out, 1'b1, S0_out, S1_out, not_3_out, S3_out);
  and and_15 (and_15_out, 1'b1, S0_out, S1_out, S2_out, not_4_out);
  and and_16 (and_16_out, 1'b1, S0_out, S1_out, S2_out, S3_out);
  nor nor_1 (S, and_4_out, and_6_out, and_7_out, and_10_out, and_11_out, and_13_out, and_16_out);
endmodule
