// Logisim project codeur+soustracteur.circ as structural Verilog: 1 circuit, main circuit main
module main (
  input  E0,
  input  E1,
  input  E2,
  input  E3,
  input  E4,
  input  E5,
  input  E6,
  input  E7,
  input  E8,
  input  E9,
  input  E10,
  input  E11,
  input  A,
  input  B,
  input  E12,
  input  E13,
  input  E14,
  input  A_2,
  input  E15,
  input  B_2,
  input  E0_2,
  input  E1_2,
  input  A_3,
  input  E2_2,
  input  B_3,
  input  E3_2,
  input  E4_2,
  input  E5_2,
  input  A_4,
  input  B_4,
  input  E6_2,
  input  E7_2,
  input  E8_2,
  input  E9_2,
  input  E10_2,
  input  E11_2,
  input  E12_2,
  input  E13_2,
  input  E14_2,
  input  E15_2,
  output out_41,
  output out_42,
  output out_43,
  output out_44,
  output out_45,
  output out_46,
  output out_47,
  output out_48
);

  wire and_1_out, and_2_out, and_3_out, and_4_out, and_5_out, and_6_out, and_7_out, and_8_out, and_9_out,
       and_10_out, and_11_out, and_12_out, and_13_out, and_14_out, and_15_out, not_1_out, not_2_out,
       not_3_out, not_4_out, not_5_out, not_6_out, not_7_out, not_8_out, not_9_out, not_10_out, not_11_out,
       not_12_out, not_13_out, not_14_out, not_15_out, S0_2_out, S0_out, S1_2_out, S1_out, S2_2_out, S2_out,
       S3_2_out, S3_out, xor_1_out, xor_2_out, xor_3_out, xor_4_out, xor_5_out, xor_6_out, xor_9_out,
       xor_11_out, xor_13_out, xor_15_out, xor_17_out, xor_19_out, xor_20_out, xor_21_out;

  or S0 (S0_out, E1_2, E3_2, E5_2, E7_2, E9_2, E11_2, E13_2, E15_2);
  or S2 (S2_out, E5_2, E4_2, E6_2, E7_2, E12_2, E13_2, E14_2, E15_2);
  or S0_2 (S0_2_out, E1, E3, E5, E7, E9, E11, E13, E15);
  or S1 (S1_out, E2, E3, E6, E7, E10, E11, E14, E15);
  or S2_2 (S2_2_out, E5, E4, E6, E7, E12, E13, E14, E15);
  or S3 (S3_out, E9, E10, E11, E12, E13, E14, E15, E8);
  or S1_2 (S1_2_out, E2_2, E3_2, E6_2, E7_2, E10_2, E11_2, E14_2, E15_2);
  or S3_2 (S3_2_out, E9_2, E10_2, E11_2, E12_2, E13_2, E14_2, E15_2, E8_2);
  not not_1 (not_1_out, S0_2_out);
  xor xor_1 (xor_1_out, S1_out, S1_2_out);
  not not_2 (not_2_out, xor_1_out);
  not not_3 (not_3_out, S1_out);
  xor xor_2 (xor_2_out, S2_2_out, S2_out);
  not not_4 (not_4_out, xor_2_out);
  and and_1 (and_1_out, not_4_out, xor_9_out);
  not not_5 (not_5_out, S2_2_out);
  and and_2 (and_2_out, not_5_out, S2_out);
  xor xor_3 (xor_3_out, S3_out, S3_2_out);
  not not_6 (not_6_out, xor_3_out);
  and and_3 (and_3_out, not_6_out, xor_11_out);
  not not_7 (not_7_out, S3_out);
  and and_4 (and_4_out, not_7_out, S3_2_out);
  xor xor_4 (xor_4_out, A, B);
  not not_8 (not_8_out, xor_4_out);
  and and_5 (and_5_out, not_8_out, xor_13_out);
  not not_9 (not_9_out, A);
  and and_6 (and_6_out, not_9_out, B);
  xor xor_5 (xor_5_out, A_2, B_2);
  not not_10 (not_10_out, xor_5_out);
  and and_7 (and_7_out, not_10_out, xor_15_out);
  not not_11 (not_11_out, A_2);
  and and_8 (and_8_out, not_11_out, B_2);
  xor xor_6 (xor_6_out, A_3, B_3);
  not not_12 (not_12_out, xor_6_out);
  and and_9 (and_9_out, not_12_out, xor_17_out);
  not not_13 (not_13_out, A_3);
  and and_10 (and_10_out, not_13_out, B_3);
  not not_14 (not_14_out, xor_20_out);
  not not_15 (not_15_out, A_4);
  xor xor_7 (out_41, S0_2_out, S0_out);
  and and_11 (and_11_out, not_1_out, S0_out);
  xor xor_8 (out_42, xor_1_out, and_11_out);
  and and_12 (and_12_out, not_2_out, and_11_out);
  xor xor_9 (xor_9_out, and_12_out, and_13_out);
  and and_13 (and_13_out, not_3_out, S1_2_out);
  xor xor_10 (out_43, xor_2_out, xor_9_out);
  xor xor_11 (xor_11_out, and_1_out, and_2_out);
  xor xor_12 (out_44, xor_3_out, xor_11_out);
  xor xor_13 (xor_13_out, and_3_out, and_4_out);
  xor xor_14 (out_45, xor_4_out, xor_13_out);
  xor xor_15 (xor_15_out, and_5_out, and_6_out);
  xor xor_16 (out_46, xor_5_out, xor_15_out);
  xor xor_17 (xor_17_out, and_7_out, and_8_out);
  xor xor_18 (out_47, xor_6_out, xor_17_out);
  xor xor_19 (xor_19_out, and_9_out, and_10_out);
  xor xor_20 (xor_20_out, A_4, B_4);
  and and_14 (and_14_out, not_14_out, xor_19_out);
  xor xor_21 (xor_21_out, and_14_out, and_15_out);
  and and_15 (and_15_out, not_15_out, B_4);
  xor xor_22 (out_48, xor_20_out, xor_19_out);
endmodule
