// Logisim project codeur_4_bits.circ as structural Verilog: 1 circuit, main circuit main
module main (
  input  E0,
  input  E1,
  input  E2,
  input  E3,
  input  E4,
  input  E5,
  input  E6,
  input  E7,
  input  E8,
  input  E9,
  input  E10,
  input  E11,
  input  E12,
  input  E13,
  input  E14,
  input  E15,
  output out_17,
  output out_18,
  output out_19,
  output out_20
);

  or S0 (out_17, E1, E3, E5, E7, E9, E11, E13, E15);
  or S1 (out_18, E2, E3, E6, E7, E10, E11, E14, E15);
  or S2 (out_19, E5, E4, E6, E7, E12, E13, E14, E15);
  or S3 (out_20, E9, E10, E11, E12, E13, E14, E15, E8);
endmodule
