// Logisim project Exo1_TP2.circ as structural Verilog: 1 circuit, main circuit main
module main (
  input  A,
  input  B,
  input  Cin,
  input  F0,
  input  F1,
  output S,
  output Cout
);

  wire and_1_out, and_2_out, and_3_out, and_4_out, and_5_out, and_6_out, and_7_out, and_8_out, and_9_out,
       and_10_out, and_11_out, and_12_out, and_13_out, and_14_out, not_1_out, not_2_out, not_3_out,
       not_4_out, not_5_out, xor_1_out, xor_2_out, xor_3_out, xor_4_out, xor_5_out, xor_6_out;

  not not_1 (not_1_out, F0);
  not not_2 (not_2_out, F1);
  and and_1 (and_1_out, A, not_1_out, not_2_out);
  and and_2 (and_2_out, B, not_1_out, not_2_out);
  and and_3 (and_3_out, Cin, not_2_out, not_1_out);
  xor xor_1 (xor_1_out, and_1_out, and_2_out);
  and and_4 (and_4_out, and_3_out, xor_1_out);
  and and_5 (and_5_out, and_1_out, and_2_out);
  xor xor_2 (xor_2_out, xor_1_out, and_3_out);
  xor xor_3 (xor_3_out, and_4_out, and_5_out);
  and and_6 (and_6_out, not_1_out, F1);
  and and_7 (and_7_out, A, not_1_out, F1);
  and and_8 (and_8_out, Cin, F1, not_1_out);
  not not_3 (not_3_out, and_7_out);
  and and_9 (and_9_out, B, F0, not_2_out);
  and and_10 (and_10_out, and_9_out, and_13_out);
  xor xor_4 (xor_4_out, and_7_out, and_6_out);
  not not_4 (not_4_out, xor_4_out);
  xor xor_5 (xor_5_out, xor_4_out, and_8_out);
  and and_11 (and_11_out, not_4_out, and_8_out);
  xor xor_6 (xor_6_out, and_11_out, and_12_out);
  and and_12 (and_12_out, not_3_out, and_6_out);
  not not_5 (not_5_out, A);
  and and_13 (and_13_out, A, F0, not_2_out);
  and and_14 (and_14_out, not_5_out, F0, F1);
  or or_1 (Cout, xor_6_out, xor_3_out);
  or or_2 (S, and_14_out, and_10_out, xor_5_out, xor_2_out);

  // Notes on the sheet:
  //   additionneur
  //   ET
  //   Soustracteur
endmodule
