// Logisim project Exo2_TP2.circ as structural Verilog: 1 circuit, main circuit main
// Count
module main (
  input  A,
  input  A_2,
  input  A_3,
  input  A_4,
  input  B,
  input  B_2,
  input  B_3,
  input  B_4,
  input  Cin,
  input  F0,
  input  F1,
  output out_12,
  output S,
  output S_2,
  output S_3,
  output S_4
);

  wire ad_2_out, ad_3_out, ad_4_out, ad_5_out, ad_6_out, ad_7_out, ad_8_out, ad_9_out, ad_10_out, ad_11_out,
       ad_12_out, ad_13_out, ad_14_out, ad_15_out, ad_16_out, ad_17_out, and_1_out, and_2_out, and_3_out,
       and_4_out, and_5_out, and_6_out, and_7_out, and_8_out, and_9_out, and_10_out, and_11_out, and_12_out,
       and_13_out, and_14_out, and_15_out, and_16_out, and_17_out, and_18_out, and_19_out, and_20_out,
       C0_out, C1_out, C2_out, ET_2_out, ET_3_out, ET_4_out, ET_5_out, ET_6_out, ET_7_out, ET_8_out,
       ET_9_out, non_2_out, non_3_out, non_4_out, non_5_out, not_1_out, not_2_out, not_3_out, not_4_out,
       not_5_out, not_6_out, not_7_out, not_8_out, not_9_out, not_10_out, not_11_out, not_12_out, not_13_out,
       not_14_out, not_15_out, not_16_out, not_17_out, not_18_out, not_19_out, not_20_out, sous_2_out,
       sous_3_out, sous_4_out, sous_5_out, sous_6_out, sous_7_out, sous_8_out, sous_9_out, sous_10_out,
       sous_11_out, sous_12_out, sous_13_out, sous_14_out, sous_15_out, sous_16_out, sous_17_out, xor_1_out,
       xor_2_out, xor_3_out, xor_4_out, xor_5_out, xor_6_out, xor_7_out, xor_8_out, xor_9_out, xor_10_out,
       xor_11_out, xor_12_out, xor_13_out, xor_14_out, xor_15_out, xor_16_out, xor_17_out, xor_18_out,
       xor_19_out, xor_20_out, xor_21_out, xor_22_out, xor_23_out, xor_24_out;

  // AND_Gate ad is placed but not wired
  // AND_Gate sous is placed but not wired
  // AND_Gate ET is placed but not wired
  // AND_Gate non is placed but not wired
  not not_1 (not_1_out, F0);
  not not_2 (not_2_out, F1);
  and ad_2 (ad_2_out, A, not_1_out, not_2_out);
  and ad_3 (ad_3_out, B, not_1_out, not_2_out);
  and ad_4 (ad_4_out, not_2_out, not_1_out, Cin);
  xor xor_1 (xor_1_out, ad_2_out, ad_3_out);
  and and_1 (and_1_out, ad_4_out, xor_1_out);
  and and_2 (and_2_out, ad_2_out, ad_3_out);
  and sous_2 (sous_2_out, F1, not_1_out, Cin);
  xor xor_2 (xor_2_out, xor_1_out, ad_4_out);
  xor xor_3 (xor_3_out, and_1_out, and_2_out);
  and sous_3 (sous_3_out, A, not_1_out, F1);
  and sous_4 (sous_4_out, B, not_1_out, F1);
  not not_3 (not_3_out, sous_3_out);
  and ET_2 (ET_2_out, B, F0, not_2_out);
  and and_3 (and_3_out, ET_2_out, ET_3_out);
  xor xor_4 (xor_4_out, sous_3_out, sous_4_out);
  xor xor_5 (xor_5_out, xor_4_out, sous_2_out);
  not not_4 (not_4_out, xor_4_out);
  and and_4 (and_4_out, not_4_out, sous_2_out);
  xor xor_6 (xor_6_out, and_4_out, and_5_out);
  and and_5 (and_5_out, not_3_out, sous_4_out);
  not not_5 (not_5_out, A);
  and non_2 (non_2_out, not_5_out, F0, F1);
  and ET_3 (ET_3_out, A, F0, not_2_out);
  and sous_5 (sous_5_out, not_1_out, F1, xor_6_out);
  or or_1 (S, non_2_out, and_3_out, xor_5_out, xor_2_out);
  or C0 (C0_out, sous_5_out, ad_5_out);
  and ad_5 (ad_5_out, not_1_out, not_2_out, xor_3_out);
  not not_6 (not_6_out, F0);
  not not_7 (not_7_out, F1);
  and ad_6 (ad_6_out, B_2, not_6_out, not_7_out);
  and ad_7 (ad_7_out, A_2, not_6_out, not_7_out);
  xor xor_7 (xor_7_out, ad_7_out, ad_6_out);
  and ad_8 (ad_8_out, not_7_out, not_6_out, C0_out);
  and and_6 (and_6_out, ad_8_out, xor_7_out);
  and and_7 (and_7_out, ad_7_out, ad_6_out);
  xor xor_8 (xor_8_out, xor_7_out, ad_8_out);
  xor xor_9 (xor_9_out, and_6_out, and_7_out);
  and sous_6 (sous_6_out, A_2, not_6_out, F1);
  and sous_7 (sous_7_out, B_2, not_6_out, F1);
  and sous_8 (sous_8_out, F1, not_6_out, C0_out);
  and ET_4 (ET_4_out, B_2, F0, not_7_out);
  xor xor_10 (xor_10_out, sous_6_out, sous_7_out);
  not not_8 (not_8_out, xor_10_out);
  and and_8 (and_8_out, not_8_out, sous_8_out);
  not not_9 (not_9_out, sous_6_out);
  and and_9 (and_9_out, not_9_out, sous_7_out);
  not not_10 (not_10_out, A_2);
  and ET_5 (ET_5_out, A_2, F0, not_7_out);
  and and_10 (and_10_out, ET_4_out, ET_5_out);
  xor xor_11 (xor_11_out, xor_10_out, sous_8_out);
  xor xor_12 (xor_12_out, and_8_out, and_9_out);
  and non_3 (non_3_out, not_10_out, F0, F1);
  and sous_9 (sous_9_out, not_6_out, F1, xor_12_out);
  or or_2 (S_2, non_3_out, and_10_out, xor_11_out, xor_8_out);
  or C1 (C1_out, sous_9_out, ad_9_out);
  and ad_9 (ad_9_out, not_6_out, not_7_out, xor_9_out);
  not not_11 (not_11_out, F0);
  not not_12 (not_12_out, F1);
  and ad_10 (ad_10_out, A_3, not_11_out, not_12_out);
  and ad_11 (ad_11_out, B_3, not_11_out, not_12_out);
  and ad_12 (ad_12_out, not_12_out, not_11_out, C1_out);
  xor xor_13 (xor_13_out, ad_10_out, ad_11_out);
  xor xor_14 (xor_14_out, xor_13_out, ad_12_out);
  and and_11 (and_11_out, ad_12_out, xor_13_out);
  xor xor_15 (xor_15_out, and_11_out, and_12_out);
  and and_12 (and_12_out, ad_10_out, ad_11_out);
  and sous_10 (sous_10_out, B_3, not_11_out, F1);
  and sous_11 (sous_11_out, F1, not_11_out, C1_out);
  and sous_12 (sous_12_out, A_3, not_11_out, F1);
  not not_13 (not_13_out, xor_16_out);
  not not_14 (not_14_out, sous_12_out);
  and ET_6 (ET_6_out, B_3, F0, not_12_out);
  and ET_7 (ET_7_out, A_3, F0, not_12_out);
  and and_13 (and_13_out, ET_6_out, ET_7_out);
  xor xor_16 (xor_16_out, sous_12_out, sous_10_out);
  xor xor_17 (xor_17_out, xor_16_out, sous_11_out);
  and and_14 (and_14_out, not_13_out, sous_11_out);
  xor xor_18 (xor_18_out, and_14_out, and_15_out);
  and and_15 (and_15_out, not_14_out, sous_10_out);
  not not_15 (not_15_out, A_3);
  and non_4 (non_4_out, not_15_out, F0, F1);
  or or_3 (S_3, non_4_out, and_13_out, xor_17_out, xor_14_out);
  and sous_13 (sous_13_out, not_11_out, F1, xor_18_out);
  and ad_13 (ad_13_out, not_11_out, not_12_out, xor_15_out);
  not not_16 (not_16_out, F0);
  not not_17 (not_17_out, F1);
  or C2 (C2_out, sous_13_out, ad_13_out);
  and ad_14 (ad_14_out, B_4, not_16_out, not_17_out);
  and ad_15 (ad_15_out, A_4, not_16_out, not_17_out);
  and ad_16 (ad_16_out, not_17_out, not_16_out, C2_out);
  xor xor_19 (xor_19_out, ad_15_out, ad_14_out);
  and and_16 (and_16_out, ad_16_out, xor_19_out);
  and and_17 (and_17_out, ad_15_out, ad_14_out);
  and sous_14 (sous_14_out, F1, not_16_out, C2_out);
  xor xor_20 (xor_20_out, xor_19_out, ad_16_out);
  xor xor_21 (xor_21_out, and_16_out, and_17_out);
  and sous_15 (sous_15_out, B_4, not_16_out, F1);
  and sous_16 (sous_16_out, A_4, not_16_out, F1);
  not not_18 (not_18_out, sous_16_out);
  and ET_8 (ET_8_out, B_4, F0, not_17_out);
  and and_18 (and_18_out, ET_8_out, ET_9_out);
  xor xor_22 (xor_22_out, sous_16_out, sous_15_out);
  xor xor_23 (xor_23_out, xor_22_out, sous_14_out);
  not not_19 (not_19_out, xor_22_out);
  and and_19 (and_19_out, not_19_out, sous_14_out);
  xor xor_24 (xor_24_out, and_19_out, and_20_out);
  and and_20 (and_20_out, not_18_out, sous_15_out);
  not not_20 (not_20_out, A_4);
  and ET_9 (ET_9_out, A_4, F0, not_17_out);
  and non_5 (non_5_out, not_20_out, F0, F1);
  and sous_17 (sous_17_out, not_16_out, F1, xor_24_out);
  or or_4 (S_4, non_5_out, and_18_out, xor_23_out, xor_20_out);
  or C3 (out_12, sous_17_out, ad_17_out);
  and ad_17 (ad_17_out, not_16_out, not_17_out, xor_21_out);

  // Notes on the sheet:
  //   FILTRE ADDITIONNEUR
  //   FILTRE SOUSTRACTEUR
  //   FILTRE A ET B
  //   FILTRE NON A
  //   additionneur
  //   Soustracteur
  //   additionneur
  //   Soustracteur
  //   ET
  //   additionneur
  //   Soustracteur
  //   ET
  //   additionneur
  //   ET
  //   Soustracteur
endmodule
