// Logisim project Exo3_TP2.circ as structural Verilog: 1 circuit, main circuit main
module main (
  input  A,
  input  in_2,
  input  in_3,
  input  in_4,
  input  B,
  input  in_6,
  input  in_7,
  input  in_8,
  input  Cin,
  input  F0,
  input  F1,
  output out_12,
  output S,
  output S_2,
  output S_3,
  output S_4
);

  wire ad_2_out, ad_3_out, ad_4_out, ad_5_out, ad_6_out, ad_7_out, ad_8_out, ad_9_out, ad_10_out, ad_11_out,
       ad_12_out, ad_13_out, ad_14_out, ad_15_out, ad_16_out, ad_17_out, and_1_out, and_2_out, and_3_out,
       and_4_out, and_5_out, and_6_out, and_7_out, and_8_out, and_9_out, and_10_out, and_11_out, and_12_out,
       and_13_out, and_14_out, and_15_out, and_16_out, and_17_out, and_18_out, and_19_out, and_20_out,
       and_21_out, and_22_out, C0_2_out, C0_out, DIV_2_out, DIV_3_out, DIV_4_out, MUL_2_out, MUL_3_out,
       MUL_4_out, not_1_out, not_2_out, not_3_out, not_4_out, not_5_out, not_6_out, not_7_out, not_8_out,
       not_9_out, not_10_out, or_4_out, sous_2_out, sous_3_out, sous_4_out, sous_5_out, sous_6_out,
       sous_7_out, sous_8_out, sous_9_out, sous_10_out, sous_11_out, sous_12_out, sous_13_out, sous_14_out,
       sous_15_out, sous_16_out, sous_17_out, xor_1_out, xor_2_out, xor_3_out, xor_4_out, xor_5_out,
       xor_6_out, xor_7_out, xor_8_out, xor_9_out, xor_10_out, xor_11_out, xor_12_out, xor_13_out,
       xor_14_out, xor_15_out, xor_16_out, xor_17_out, xor_18_out, xor_19_out, xor_20_out, xor_21_out,
       xor_22_out, xor_23_out, xor_24_out;

  // AND_Gate ad is placed but not wired
  // AND_Gate sous is placed but not wired
  // AND_Gate DIV is placed but not wired
  // AND_Gate MUL is placed but not wired
  not not_1 (not_1_out, F0);
  not not_2 (not_2_out, F1);
  and ad_2 (ad_2_out, B, not_1_out, not_2_out);
  and ad_3 (ad_3_out, A, not_1_out, not_2_out);
  and ad_4 (ad_4_out, not_2_out, not_1_out, Cin);
  xor xor_1 (xor_1_out, ad_3_out, ad_2_out);
  and and_1 (and_1_out, ad_4_out, xor_1_out);
  and and_2 (and_2_out, ad_3_out, ad_2_out);
  and sous_2 (sous_2_out, F1, not_1_out, Cin);
  xor xor_2 (xor_2_out, xor_1_out, ad_4_out);
  xor xor_3 (xor_3_out, and_1_out, and_2_out);
  and sous_3 (sous_3_out, B, not_1_out, F1);
  and sous_4 (sous_4_out, A, not_1_out, F1);
  not not_3 (not_3_out, sous_4_out);
  and MUL_2 (MUL_2_out, F0, not_2_out);
  and and_3 (and_3_out, A, MUL_2_out);
  xor xor_4 (xor_4_out, sous_4_out, sous_3_out);
  not not_4 (not_4_out, xor_4_out);
  xor xor_5 (xor_5_out, xor_4_out, sous_2_out);
  and and_4 (and_4_out, not_4_out, sous_2_out);
  xor xor_6 (xor_6_out, and_4_out, and_5_out);
  and and_5 (and_5_out, not_3_out, sous_3_out);
  and ad_5 (ad_5_out, not_1_out, not_2_out, xor_3_out);
  and sous_5 (sous_5_out, F1, not_1_out, xor_6_out);
  or or_1 (S, and_10_out, xor_5_out, xor_2_out);
  or C0 (C0_out, sous_5_out, ad_5_out);
  and ad_6 (ad_6_out, in_6, not_1_out, not_2_out);
  and ad_7 (ad_7_out, not_2_out, not_1_out, C0_out);
  and ad_8 (ad_8_out, in_2, not_1_out, not_2_out);
  xor xor_7 (xor_7_out, ad_8_out, ad_6_out);
  and and_6 (and_6_out, ad_7_out, xor_7_out);
  and and_7 (and_7_out, ad_8_out, ad_6_out);
  xor xor_8 (xor_8_out, xor_7_out, ad_7_out);
  xor xor_9 (xor_9_out, and_6_out, and_7_out);
  and sous_6 (sous_6_out, in_6, not_1_out, F1);
  and sous_7 (sous_7_out, in_2, not_1_out, F1);
  and sous_8 (sous_8_out, F1, not_1_out, C0_out);
  xor xor_10 (xor_10_out, sous_7_out, sous_6_out);
  not not_5 (not_5_out, xor_10_out);
  and and_8 (and_8_out, not_5_out, sous_8_out);
  not not_6 (not_6_out, sous_7_out);
  and and_9 (and_9_out, not_6_out, sous_6_out);
  and DIV_2 (DIV_2_out, F0, F1);
  xor xor_11 (xor_11_out, xor_10_out, sous_8_out);
  xor xor_12 (xor_12_out, and_8_out, and_9_out);
  and MUL_3 (MUL_3_out, F0, not_2_out);
  and and_10 (and_10_out, DIV_2_out, in_2);
  and and_11 (and_11_out, in_2, MUL_3_out);
  or or_2 (S_2, and_16_out, and_3_out, xor_11_out, xor_8_out);
  and sous_9 (sous_9_out, F1, not_1_out, xor_12_out);
  or C0_2 (C0_2_out, sous_9_out, ad_9_out);
  and ad_9 (ad_9_out, not_1_out, not_2_out, xor_9_out);
  and ad_10 (ad_10_out, in_7, not_1_out, not_2_out);
  and ad_11 (ad_11_out, in_3, not_1_out, not_2_out);
  xor xor_13 (xor_13_out, ad_11_out, ad_10_out);
  and ad_12 (ad_12_out, not_2_out, not_1_out, C0_2_out);
  and and_12 (and_12_out, ad_12_out, xor_13_out);
  and and_13 (and_13_out, ad_11_out, ad_10_out);
  xor xor_14 (xor_14_out, xor_13_out, ad_12_out);
  xor xor_15 (xor_15_out, and_12_out, and_13_out);
  and sous_10 (sous_10_out, in_7, not_1_out, F1);
  and sous_11 (sous_11_out, in_3, not_1_out, F1);
  and sous_12 (sous_12_out, F1, not_1_out, C0_2_out);
  xor xor_16 (xor_16_out, sous_11_out, sous_10_out);
  not not_7 (not_7_out, xor_16_out);
  and and_14 (and_14_out, not_7_out, sous_12_out);
  not not_8 (not_8_out, sous_11_out);
  and and_15 (and_15_out, not_8_out, sous_10_out);
  xor xor_17 (xor_17_out, xor_16_out, sous_12_out);
  xor xor_18 (xor_18_out, and_14_out, and_15_out);
  and DIV_3 (DIV_3_out, F0, F1);
  and MUL_4 (MUL_4_out, F0, not_2_out);
  and and_16 (and_16_out, DIV_3_out, in_3);
  and and_17 (and_17_out, in_3, MUL_4_out);
  or or_3 (S_3, and_22_out, and_11_out, xor_17_out, xor_14_out);
  and sous_13 (sous_13_out, F1, not_1_out, xor_18_out);
  or or_4 (or_4_out, sous_13_out, ad_13_out);
  and ad_13 (ad_13_out, not_1_out, not_2_out, xor_15_out);
  and ad_14 (ad_14_out, in_4, not_1_out, not_2_out);
  and ad_15 (ad_15_out, in_8, not_1_out, not_2_out);
  and ad_16 (ad_16_out, not_2_out, not_1_out, or_4_out);
  xor xor_19 (xor_19_out, ad_14_out, ad_15_out);
  xor xor_20 (xor_20_out, xor_19_out, ad_16_out);
  and and_18 (and_18_out, ad_16_out, xor_19_out);
  xor xor_21 (xor_21_out, and_18_out, and_19_out);
  and and_19 (and_19_out, ad_14_out, ad_15_out);
  and sous_14 (sous_14_out, in_8, not_1_out, F1);
  and sous_15 (sous_15_out, F1, not_1_out, or_4_out);
  and sous_16 (sous_16_out, in_4, not_1_out, F1);
  xor xor_22 (xor_22_out, sous_16_out, sous_14_out);
  not not_9 (not_9_out, xor_22_out);
  and and_20 (and_20_out, not_9_out, sous_15_out);
  not not_10 (not_10_out, sous_16_out);
  and and_21 (and_21_out, not_10_out, sous_14_out);
  and DIV_4 (DIV_4_out, F0, F1);
  and and_22 (and_22_out, DIV_4_out, in_4);
  xor xor_23 (xor_23_out, xor_22_out, sous_15_out);
  xor xor_24 (xor_24_out, and_20_out, and_21_out);
  and ad_17 (ad_17_out, not_2_out, not_1_out, xor_21_out);
  or or_5 (S_4, and_17_out, xor_23_out, xor_20_out);
  xor xor_25 (out_12, ad_17_out, sous_17_out);
  and sous_17 (sous_17_out, F1, not_1_out, xor_24_out);

  // Notes on the sheet:
  //   FILTRE ADDITIONNEUR
  //   FILTRE SOUSTRACTEUR
  //   FILTRE A / 2
  //   FILTRE A x 2
  //   additionneur
  //   Soustracteur
  //   additionneur
  //   Soustracteur
  //   additionneur
  //   Soustracteur
  //   additionneur
  //   Soustracteur
endmodule
